# Fritzing sketch clock_0 (saved by Fritzing 0.8.7b)
circuit board: 9.9cm x 3.3cm
breadboards: 1

parts:
  DS1307_RTC = DS1307 [package=THT]
  Bat_CR2032 = Battery Holders [part_number="CR2032 3V" package=battcom_20mm_pth]
  13kHz = CRYSTAL - kHz [frequency="32 kHz" part_number="32kHz Quartz"]
  10k = Resistor [tolerance=±5% resistance=10k package=THT]
  10k_2 = Resistor [tolerance=±5% resistance=10k package=THT]
  Bluetooth = Generic Bluetooth Dongle - 4pin [part_number="Bluetooth Dongle" package=THT]
  8x8_Matrix = Generic 8x8 LED Matrix (Shift register) [part_number="8x8 LED Matrix (Shift register)" package=THT]
  Brightn = Rotary Potentiometer (Large) [maximum_resistance=100kΩ package=THT]
  Btn_2 = Generic male header - 2 pins [form="♂ (male)" package=THT]
  Btn_1 = Generic male header - 2 pins [form="♂ (male)" package=THT]
  Byps = Generic male header - 2 pins [form="♂ (male)" package=THT]
  MCU_(Arduino_nano) = Arduino Nano (Rev3.0)
  part = Rotary Potentiometer (Large) [maximum_resistance=100kΩ package=THT]  # not connected

nets:
  N1: DS1307_RTC.X1_-_Crystal, 13kHz.pin_0
  N2: DS1307_RTC.X2_-_Crystal, 13kHz.pin_1
  N3: DS1307_RTC.Vbat_-_Backup_Supply, Bat_CR2032.+
  GND: DS1307_RTC.0V, Bat_CR2032.-, Bluetooth.GND, 8x8_Matrix.GND, Brightn.leg2, Btn_2.GND, Btn_1.GND, Byps.GND, MCU_(Arduino_nano).GND
  N4: DS1307_RTC.SDA_-_I2C_Data, 10k.Pin_0, MCU_(Arduino_nano).A4
  N5: DS1307_RTC.SCL_-_I2C_Clock, 10k_2.Pin_0, MCU_(Arduino_nano).A5
  VCC: DS1307_RTC.+V, 10k.Pin_1, 10k_2.Pin_1, Bluetooth.VCC, Brightn.leg1, MCU_(Arduino_nano).5V
  N6: Bluetooth.RXD, MCU_(Arduino_nano).D10
  N7: Bluetooth.TXD, MCU_(Arduino_nano).D11/MOSI
  N8: 8x8_Matrix.VCC, Brightn.wiper
  N9: 8x8_Matrix.LE, MCU_(Arduino_nano).D2
  N10: 8x8_Matrix.CK, MCU_(Arduino_nano).D3
  N11: 8x8_Matrix.DI, MCU_(Arduino_nano).D4
  N12: Btn_2.SIG, MCU_(Arduino_nano).D6
  N13: Btn_1.SIG, MCU_(Arduino_nano).D5
  N14: Byps.SIG, MCU_(Arduino_nano).D7

notes:
  VCC
  GND
  TXD
  RXD
  SIG
  +3V
  -0V
  Mount on back!
  Mount here
  LE
  CK
  K0
  8x8 Matrix

custom parts:
  Generic Bluetooth Dongle - 4pin: China Bluetooth dongle
  Generic 8x8 LED Matrix (Shift register): 8x8 LED Matrix (Shift register) 8x8 LED Matrix using two shift registers
  Generic male header - 2 pins: Generic male header
  Arduino Nano (Rev3.0): The Arduino Nano is a small, complete, and breadboard-friendly board based on the ATmega328 (Arduino Nano 3.0) or ATmega168 (Arduino Nano 2.x). It has more or less the same functionality of the Arduino Duemilanove, but in a different package. It lacks only a DC power jack, and works with a Mini-B USB cable instead of a standard one. The Nano was designed and is being produced by Gravitech.
